// Logisim project OBC8421_6.circ as structural Verilog: 1 circuit, main circuit main
module main (
  input  A,
  input  B,
  input  C,
  input  D,
  output A_2,
  output B_2,
  output C_2,
  output D_2
);

  wire and_1_out, and_2_out, and_3_out, and_4_out, and_5_out, and_6_out, and_7_out, and_8_out, and_9_out,
       not_1_out, not_2_out, not_3_out;

  // Probe on {A, B, C, D}
  not not_1 (not_1_out, B);
  not not_2 (not_2_out, C);
  not not_3 (not_3_out, A);
  and and_1 (and_1_out, not_3_out, C);
  and and_2 (and_2_out, not_3_out, B);
  and and_3 (and_3_out, not_3_out, B, C);
  and and_4 (and_4_out, not_1_out, not_2_out);
  and and_5 (and_5_out, not_3_out, not_2_out);
  and and_6 (and_6_out, not_1_out, not_2_out);
  and and_7 (and_7_out, not_1_out, not_2_out, D);
  and and_8 (and_8_out, not_3_out, D);
  and and_9 (and_9_out, A, not_1_out, not_2_out);
  or or_1 (B_2, and_3_out, and_4_out);
  or or_2 (C_2, and_5_out, and_6_out);
  or or_3 (D_2, and_7_out, and_8_out);
  or or_4 (A_2, and_1_out, and_2_out, and_9_out);
  // Probe on {A_2, B_2, C_2, D_2}
endmodule
