// Logisim project Binary_Counter.circ as structural Verilog: 1 circuit, main circuit main
module main (
  input  V
);

  wire and_1_out, and_2_out, and_3_out, clock_1_out, nQ1_out, nQ2_out;
  wire [2:0] t_ff_3_q;

  not nQ2 (nQ2_out, t_ff_3_q[1]);
  not nQ1 (nQ1_out, t_ff_3_q[0]);
  and and_1 (and_1_out, nQ2_out, V, nQ1_out);
  Clock clock_1 (.out(clock_1_out));
  and and_2 (and_2_out, V, nQ1_out);
  buf and_3 (and_3_out, V);  // AND_Gate
  T_Flip_Flop t_ff_1 (.clk(clock_1_out), .T(and_1_out), .Q(t_ff_3_q[2]));  // open: Qn, preset, reset, en
  T_Flip_Flop t_ff_2 (.clk(clock_1_out), .T(and_2_out), .Q(t_ff_3_q[1]));  // open: Qn, preset, reset, en
  T_Flip_Flop t_ff_3 (.clk(clock_1_out), .T(and_3_out), .Q(t_ff_3_q[0]));  // open: Qn, preset, reset, en
  // Probe on t_ff_3_q

  // Notes on the sheet:
  //   Q3
  //   Q1
  //   Q2
endmodule
